// Logisim project b8_a2_a.circ as structural Verilog: 1 circuit, main circuit main
module main (
);

  wire A_q, A_qn, B_q, B_qn, clock_1_out, or_1_out, or_2_out;

  Clock clock_1 (.out(clock_1_out));
  or or_1 (or_1_out, B_q, A_qn);
  or or_2 (or_2_out, B_q, A_q);
  T_Flip_Flop B (.clk(clock_1_out), .T(or_1_out), .Q(B_q), .Qn(B_qn));  // open: preset, reset, en
  T_Flip_Flop A (.clk(clock_1_out), .T(or_2_out), .Q(A_q), .Qn(A_qn));  // open: preset, reset, en
endmodule
