// Logisim project b8_a4.circ as structural Verilog: 1 circuit, main circuit main
module main (
);

  wire and_1_out, and_2_out, and_3_out, and_4_out, and_5_out, and_6_out, and_7_out, and_8_out, and_9_out,
       and_10_out, and_11_out, and_12_out, and_13_out, and_14_out, and_15_out, and_16_out, clock_1_out,
       d_ff_1_q, d_ff_2_q, d_ff_3_q, d_ff_4_q, d_ff_5_q, d_ff_6_q, j_k_ff_1_q, j_k_ff_2_q, j_k_ff_3_q,
       j_k_ff_4_q, j_k_ff_5_q, j_k_ff_6_q, j_k_ff_7_q, j_k_ff_8_q, j_k_ff_9_q, j_k_ff_10_q, j_k_ff_11_q,
       j_k_ff_12_q, j_k_ff_13_q, j_k_ff_14_q, j_k_ff_15_q, not_1_out, not_2_out, not_3_out, or_1_out,
       or_2_out, or_3_out, or_4_out, or_5_out, R_out, S_out;

  Clock clock_1 (.out(clock_1_out));
  or or_1 (or_1_out, S_out, and_2_out);
  Button S (.out(S_out));
  Button R (.out(R_out));
  and and_1 (and_1_out, clock_1_out, j_k_ff_1_q);
  J_K_Flip_Flop j_k_ff_1 (.J(or_1_out), .clk(or_1_out), .K(or_1_out), .Q(j_k_ff_1_q));  // open: Qn, preset, en, reset
  and and_2 (and_2_out, j_k_ff_1_q, R_out);
  not not_1 (not_1_out, and_1_out);
  D_Flip_Flop d_ff_1 (.clk(not_1_out), .D(and_15_out), .Q(d_ff_1_q));  // open: Qn, preset, en, reset
  not not_2 (not_2_out, d_ff_4_q);
  D_Flip_Flop d_ff_2 (.clk(not_2_out), .D(and_12_out), .Q(d_ff_2_q));  // open: Qn, preset, en, reset
  not not_3 (not_3_out, d_ff_5_q);
  D_Flip_Flop d_ff_3 (.clk(not_3_out), .D(and_16_out), .Q(d_ff_3_q));  // open: Qn, preset, en, reset
  D_Flip_Flop d_ff_4 (.clk(and_1_out), .D(d_ff_1_q), .Q(d_ff_4_q));  // open: Qn, preset, en, reset
  D_Flip_Flop d_ff_5 (.clk(d_ff_4_q), .D(d_ff_2_q), .Q(d_ff_5_q));  // open: Qn, preset, en, reset
  D_Flip_Flop d_ff_6 (.clk(d_ff_5_q), .D(d_ff_3_q), .Q(d_ff_6_q));  // open: Qn, preset, en, reset
  J_K_Flip_Flop j_k_ff_2 (
    .J(and_1_out), .clk(and_1_out), .K(j_k_ff_2_q), .Q(j_k_ff_2_q), .reset(R_out));  // open: Qn, preset, en
  J_K_Flip_Flop j_k_ff_3 (
    .J(d_ff_4_q), .clk(d_ff_4_q), .K(j_k_ff_3_q), .Q(j_k_ff_3_q), .reset(R_out));  // open: Qn, preset, en
  J_K_Flip_Flop j_k_ff_4 (
    .J(d_ff_5_q), .clk(d_ff_5_q), .K(j_k_ff_4_q), .Q(j_k_ff_4_q), .reset(R_out));  // open: Qn, preset, en
  J_K_Flip_Flop j_k_ff_5 (
    .J(d_ff_6_q), .clk(d_ff_6_q), .K(j_k_ff_5_q), .Q(j_k_ff_5_q), .reset(R_out));  // open: Qn, preset, en
  and and_3 (and_3_out, j_k_ff_2_q, ~or_2_out);  // AND_Gate
  or or_2 (or_2_out, and_4_out, and_15_out);
  and and_4 (and_4_out, j_k_ff_2_q, j_k_ff_6_q);
  and and_5 (and_5_out, j_k_ff_3_q, ~or_3_out);  // AND_Gate
  or or_3 (or_3_out, and_6_out, and_12_out);
  and and_6 (and_6_out, j_k_ff_3_q, j_k_ff_7_q);
  and and_7 (and_7_out, j_k_ff_4_q, ~or_4_out);  // AND_Gate
  or or_4 (or_4_out, and_8_out, and_16_out);
  and and_8 (and_8_out, j_k_ff_4_q, j_k_ff_8_q);
  and and_9 (and_9_out, j_k_ff_5_q, ~or_5_out);  // AND_Gate
  or or_5 (or_5_out, and_10_out, and_14_out);
  and and_10 (and_10_out, j_k_ff_5_q, j_k_ff_9_q);
  J_K_Flip_Flop j_k_ff_6 (
    .J(and_3_out), .clk(and_1_out), .K(or_2_out), .Q(j_k_ff_6_q), .reset(R_out));  // open: Qn, preset, en
  J_K_Flip_Flop j_k_ff_7 (
    .J(and_5_out), .clk(d_ff_4_q), .K(or_3_out), .Q(j_k_ff_7_q), .reset(R_out));  // open: Qn, preset, en
  J_K_Flip_Flop j_k_ff_8 (
    .J(and_7_out), .clk(d_ff_5_q), .K(or_4_out), .Q(j_k_ff_8_q), .reset(R_out));  // open: Qn, preset, en
  J_K_Flip_Flop j_k_ff_9 (
    .J(and_9_out), .clk(d_ff_6_q), .K(or_5_out), .Q(j_k_ff_9_q), .reset(R_out));  // open: Qn, preset, en
  and and_11 (and_11_out, and_4_out, j_k_ff_10_q);
  and and_12 (and_12_out, j_k_ff_3_q, j_k_ff_11_q);
  and and_13 (and_13_out, and_8_out, j_k_ff_12_q);
  and and_14 (and_14_out, j_k_ff_5_q, j_k_ff_13_q);
  J_K_Flip_Flop j_k_ff_10 (
    .J(and_4_out), .clk(and_1_out), .K(and_11_out), .Q(j_k_ff_10_q), .reset(R_out));  // open: Qn, preset, en
  J_K_Flip_Flop j_k_ff_11 (
    .J(and_6_out), .clk(d_ff_4_q), .K(and_12_out), .Q(j_k_ff_11_q), .reset(R_out));  // open: Qn, preset, en
  J_K_Flip_Flop j_k_ff_12 (
    .J(and_8_out), .clk(d_ff_5_q), .K(and_13_out), .Q(j_k_ff_12_q), .reset(R_out));  // open: Qn, preset, en
  J_K_Flip_Flop j_k_ff_13 (
    .J(and_10_out), .clk(d_ff_6_q), .K(and_14_out), .Q(j_k_ff_13_q), .reset(R_out));  // open: Qn, preset, en
  and and_15 (and_15_out, j_k_ff_14_q, j_k_ff_2_q);
  and and_16 (and_16_out, j_k_ff_15_q, j_k_ff_4_q);
  J_K_Flip_Flop j_k_ff_14 (
    .J(and_11_out), .clk(and_1_out), .K(and_15_out), .Q(j_k_ff_14_q), .reset(R_out));  // open: Qn, preset, en
  J_K_Flip_Flop j_k_ff_15 (
    .J(and_13_out), .clk(d_ff_5_q), .K(and_16_out), .Q(j_k_ff_15_q), .reset(R_out));  // open: Qn, preset, en
endmodule
